// Logisim project HW4[1]_pipeling.circ as structural Verilog: 9 circuits, main circuit main
module main (
);

  wire and_1_out, and_2_out, and_3_out, and_4_out, and_5_out, and_6_out, and_7_out, clock_1_out,
       comparator_1_gt, control_unit_1_asrc, control_unit_1_brn, control_unit_1_dmr, control_unit_1_dmw,
       control_unit_1_j, control_unit_1_li, control_unit_1_reboot, control_unit_1_regw, control_unit_1_rra,
       control_unit_1_sia, control_unit_1_store, divider_1_out_15, divider_1_out_16, divider_2__1_bit_2,
       divider_2_out_15, divider_2_out_16, divider_2_out_17, divider_2_out_18, divider_2_out_19,
       divider_3_out_15, divider_3_out_16, divider_3_out_19, forwarding_1_r1_2, forwarding_1_r2_2,
       forwarding_2_r1_2, forwarding_2_r2_2, halter_1_h, halter_1_reboor, j_cmd_1_cond, j_cmd_1_uncond,
       multiplexer_1_out, not_1_out, not_2_out, not_3_out, or_1_out, or_2_out, or_3_out, or_4_out;
  wire [2:0] control_unit_1_aop, divider_2_out_21, divider_2_out_22, divider_3_out_22, multiplexer_3_out;
  wire [4:0] divider_2_out_23;
  wire [15:0] alu_1_out_4, bit_extender_1_out, divider_1_out_24, divider_1_out_25, divider_2_out_24,
       divider_2_out_25, divider_3_out_20, divider_3_out_24, divider_3_out_25, multiplexer_2_out,
       multiplexer_4_out, multiplexer_5_out, multiplexer_6_out, multiplexer_7_out, multiplexer_8_out,
       multiplexer_9_out, multiplexer_10_out, pc_increment_1_ins, pc_increment_1_out_9, RA_q, ram_1_data,
       ram_2_data, registers_1_r1_value, registers_1_r2_value;

  Clock clock_1 (.out(clock_1_out));
  and and_1 (and_1_out, not_3_out, divider_2__1_bit_2);
  not not_1 (not_1_out, control_unit_1_j);
  Multiplexer #(.enable("false")) multiplexer_1 (
    .in0(divider_2__1_bit_2), .in1(and_1_out), .out(multiplexer_1_out), .sel(not_1_out));
  PC_Increment pc_increment_1 (
    .br(bit_extender_1_out), .uncond(j_cmd_1_uncond), .bnch(multiplexer_1_out), .Rra(control_unit_1_rra),
    .reboot(halter_1_reboor), .ra(RA_q), .clock(and_2_out), .cond(j_cmd_1_cond),
    .out_9(pc_increment_1_out_9), .Ins(pc_increment_1_ins));
  // Probe on pc_increment_1_ins
  and and_2 (and_2_out, clock_1_out, not_2_out);
  J_cmd j_cmd_1 (.in_1(multiplexer_2_out), .uncond(j_cmd_1_uncond), .cond(j_cmd_1_cond));
  RAM #(.addrWidth(16), .dataWidth(16)) ram_1 (
    .addr(pc_increment_1_ins), .data(ram_1_data), .clk(clock_1_out));  // open: sel, ld, clr
  Multiplexer #(.width(16), .enable("false")) multiplexer_2 (
    .in0(ram_1_data), .in1(16'h4000), .out(multiplexer_2_out), .sel(divider_1_out_16));
  halter halter_1 (.in_1(multiplexer_2_out), .h(halter_1_h), .reboor(halter_1_reboor));
  or or_1 (or_1_out, divider_1_out_15, j_cmd_1_uncond);
  not not_2 (not_2_out, halter_1_h);
  Divider divider_1 (
    .clock(clock_1_out), .in_3(j_cmd_1_cond), .in_4(or_1_out), ._16_bit_2(pc_increment_1_out_9),
    ._16_bit_3(multiplexer_2_out), .out_15(divider_1_out_15), .out_16(divider_1_out_16),
    .out_24(divider_1_out_24), .out_25(divider_1_out_25));  // open: in_5, in_6, in_7, _16_bit, _3_bit, _3_bit_2, _5_bit, out_17, out_18, out_19, out_20, out_21, out_22, out_23, _1_bit, _1_bit_2
  Register #(.width(16)) RA (.D(divider_1_out_24), .en(and_3_out), .Q(RA_q), .clk(and_3_out));  // open: clr
  and and_3 (and_3_out, clock_1_out, control_unit_1_sia);
  Multiplexer #(.width(3), .enable("false")) multiplexer_3 (
    .in0(divider_1_out_25[4:2]), .in1(divider_1_out_25[10:8]), .out(multiplexer_3_out), .sel(or_2_out));
  or or_2 (or_2_out, and_4_out, control_unit_1_store);
  and and_4 (and_4_out, control_unit_1_brn, ~control_unit_1_j);  // AND_Gate
  Control_Unit control_unit_1 (
    .in_1(divider_1_out_25[15:11]), .Brn(control_unit_1_brn), .DMR(control_unit_1_dmr),
    .Aop(control_unit_1_aop), .DMW(control_unit_1_dmw), .J(control_unit_1_j), .Asrc(control_unit_1_asrc),
    .RegW(control_unit_1_regw), .SIA(control_unit_1_sia), .Rra(control_unit_1_rra), .li(control_unit_1_li),
    .reboot(control_unit_1_reboot), .store(control_unit_1_store));  // open: h
  Registers registers_1 (
    .write_signal(divider_3_out_19), .Write_Register(divider_3_out_22), .Write_Data(multiplexer_10_out),
    .R1(divider_1_out_25[7:5]), .R2(multiplexer_3_out), .Clock(clock_1_out), .R1_value(registers_1_r1_value),
    .R2_value(registers_1_r2_value));
  and and_5 (and_5_out, control_unit_1_brn, ~control_unit_1_reboot);  // AND_Gate
  Multiplexer #(.width(16), .enable("false")) multiplexer_4 (
    .in0(registers_1_r1_value), .in1(alu_1_out_4), .out(multiplexer_4_out), .sel(forwarding_1_r1_2));
  Multiplexer #(.width(16), .enable("false")) multiplexer_5 (
    .in0(registers_1_r2_value), .in1(alu_1_out_4), .out(multiplexer_5_out), .sel(forwarding_1_r2_2));
  forwarding forwarding_1 (
    .r1(divider_1_out_25[7:5]), .Dest(divider_2_out_22), .r2(multiplexer_3_out), .r1_2(forwarding_1_r1_2),
    .r2_2(forwarding_1_r2_2), .in_4(or_3_out));
  Divider divider_2 (
    .clock(clock_1_out), .in_3(control_unit_1_dmr), .in_4(control_unit_1_dmw), .in_5(control_unit_1_asrc),
    .in_6(control_unit_1_li), .in_7(control_unit_1_regw), ._3_bit(control_unit_1_aop),
    ._3_bit_2(divider_1_out_25[10:8]), ._5_bit(divider_1_out_25[4:0]), ._16_bit_2(multiplexer_6_out),
    ._16_bit_3(multiplexer_7_out), .out_15(divider_2_out_15), .out_16(divider_2_out_16),
    .out_17(divider_2_out_17), .out_18(divider_2_out_18), .out_19(divider_2_out_19),
    .out_21(divider_2_out_21), .out_22(divider_2_out_22), .out_23(divider_2_out_23),
    .out_24(divider_2_out_24), .out_25(divider_2_out_25), ._1_bit(and_5_out), ._1_bit_2(divider_2__1_bit_2));  // open: _16_bit, out_20
  Multiplexer #(.width(16), .enable("false")) multiplexer_6 (
    .in0(multiplexer_4_out), .in1(divider_3_out_24), .out(multiplexer_6_out), .sel(and_6_out));
  and and_6 (and_6_out, ~forwarding_1_r1_2, forwarding_2_r1_2);  // AND_Gate
  Multiplexer #(.width(16), .enable("false")) multiplexer_7 (
    .in0(multiplexer_5_out), .in1(divider_3_out_24), .out(multiplexer_7_out), .sel(and_7_out));
  and and_7 (and_7_out, ~forwarding_1_r2_2, forwarding_2_r2_2);  // AND_Gate
  Comparator #(.width(16)) comparator_1 (
    .a(divider_2_out_25), .b(divider_2_out_24), .gt(comparator_1_gt));  // open: eq, lt
  assign bit_extender_1_out = {{11{divider_2_out_23[4]}}, divider_2_out_23};  // Bit_Extender bit_extender_1
  or or_3 (or_3_out, divider_2_out_19, divider_2_out_16);
  not not_3 (not_3_out, comparator_1_gt);
  Multiplexer #(.width(16), .enable("false")) multiplexer_8 (
    .in0(divider_2_out_24), .in1({16{1'b0}}), .out(multiplexer_8_out), .sel(divider_2_out_18));
  Multiplexer #(.width(16), .enable("false")) multiplexer_9 (
    .in0(divider_2_out_25), .in1(bit_extender_1_out), .out(multiplexer_9_out), .sel(divider_2_out_17));
  ALU alu_1 (.R1(multiplexer_8_out), .R2(multiplexer_9_out), .op(divider_2_out_21), .out_4(alu_1_out_4));
  forwarding forwarding_2 (
    .r1(divider_1_out_25[7:5]), .Dest(divider_3_out_22), .r2(multiplexer_3_out), .r1_2(forwarding_2_r1_2),
    .r2_2(forwarding_2_r2_2), .in_4(or_4_out));
  Divider divider_3 (
    .clock(clock_1_out), .in_3(divider_2_out_15), .in_4(divider_2_out_16), .in_7(divider_2_out_19),
    ._16_bit(divider_2_out_24), ._3_bit_2(divider_2_out_22), ._16_bit_2(alu_1_out_4),
    ._16_bit_3(divider_2_out_25), .out_15(divider_3_out_15), .out_16(divider_3_out_16),
    .out_19(divider_3_out_19), .out_20(divider_3_out_20), .out_22(divider_3_out_22),
    .out_24(divider_3_out_24), .out_25(divider_3_out_25));  // open: in_5, in_6, _3_bit, _5_bit, out_17, out_18, out_21, out_23, _1_bit, _1_bit_2
  or or_4 (or_4_out, divider_3_out_16, divider_3_out_19);
  RAM #(.addrWidth(16), .dataWidth(16), .bus("separate")) ram_2 (
    .addr(divider_3_out_20), .din(divider_3_out_25), .data(ram_2_data), .str(divider_3_out_16),
    .clk(clock_1_out), .ld(divider_3_out_15));  // open: sel, clr
  Multiplexer #(.width(16), .enable("false")) multiplexer_10 (
    .in0(divider_3_out_24), .in1(ram_2_data), .out(multiplexer_10_out), .sel(divider_3_out_15));

  // Notes on the sheet:
  //   Implement LI structural hazard
  //   test forwarding unit
endmodule

module ALU (
  input  [15:0] R1,
  input  [15:0] R2,
  input  [2:0] op,
  output [15:0] out_4
);

  wire comparator_1_gt, comparator_2_lt;
  wire [15:0] adder_1_out, and_1_out, bit_extender_1_out, multiplexer_1_out, multiplexer_2_out,
       negator_1_out, or_1_out, shifter_1_out, shifter_2_out;

  Comparator #(.width(16)) comparator_1 (.a(R2), .b(16'hf), .gt(comparator_1_gt));  // open: eq, lt
  assign and_1_out = R1 & R2;  // AND_Gate and_1, 16 bits wide
  assign or_1_out = R1 | R2;  // OR_Gate or_1, 16 bits wide
  Adder #(.width(16)) adder_1 (.a(R1), .b(R2), .out(adder_1_out));  // open: cin, cout
  Negator #(.width(16)) negator_1 (.in(R1), .out(negator_1_out));
  Comparator #(.width(16)) comparator_2 (.a(R1), .b(R2), .lt(comparator_2_lt));  // open: gt, eq
  Shifter #(.width(16)) shifter_1 (.in(R1), .\dist (R2[3:0]), .out(shifter_1_out));
  Shifter #(.width(16), .shift("lr")) shifter_2 (.in(R1), .\dist (R2[3:0]), .out(shifter_2_out));
  assign bit_extender_1_out = {{15{1'b0}}, comparator_2_lt};  // Bit_Extender bit_extender_1
  Multiplexer #(.width(16), .enable("false")) multiplexer_1 (
    .in0(shifter_2_out), .in1({16{1'b0}}), .out(multiplexer_1_out), .sel(comparator_1_gt));
  Multiplexer #(.width(16), .enable("false")) multiplexer_2 (
    .in0(shifter_1_out), .in1({16{1'b0}}), .out(multiplexer_2_out), .sel(comparator_1_gt));
  Multiplexer #(.select(3), .width(16), .enable("false")) multiplexer_3 (
    .in0(multiplexer_1_out), .in1(and_1_out), .in2(or_1_out), .in3(adder_1_out), .in4(negator_1_out),
    .in5({16{1'b0}}), .in6(bit_extender_1_out), .in7(multiplexer_2_out), .out(out_4), .sel(op));
endmodule

module Control_Unit (
  input  [4:0] in_1,
  output Brn,
  output DMR,
  output [2:0] Aop,
  output DMW,
  output h,
  output J,
  output Asrc,
  output RegW,
  output SIA,
  output Rra,
  output li,
  output reboot,
  output store
);

  wire and_2_out, and_3_out, and_4_out, and_5_out, and_6_out, and_7_out, and_8_out, and_9_out, and_10_out,
       and_11_out, and_12_out, and_13_out, and_14_out, and_20_out, and_21_out, and_22_out, and_23_out,
       not_1_out, not_2_out, not_3_out, not_4_out, not_5_out, not_6_out, not_7_out, not_8_out, not_9_out,
       not_10_out, not_11_out, not_12_out, not_13_out, not_14_out, not_15_out, not_16_out, not_17_out,
       not_18_out, not_19_out, not_20_out, not_21_out, not_22_out, not_23_out, not_24_out, not_25_out,
       not_26_out, not_27_out, not_28_out, not_29_out, not_30_out, not_31_out, not_32_out, not_33_out,
       not_34_out, not_35_out, not_36_out, not_37_out, not_38_out, not_39_out, not_40_out, not_41_out,
       not_42_out, not_43_out, not_44_out, not_45_out, not_46_out, not_47_out, not_48_out;

  and and_1 (h, in_1[4], in_1[3], in_1[2], in_1[1], in_1[0]);
  not not_1 (not_1_out, in_1[4]);
  not not_2 (not_2_out, in_1[3]);
  not not_3 (not_3_out, in_1[2]);
  not not_4 (not_4_out, in_1[1]);
  not not_5 (not_5_out, in_1[0]);
  not not_6 (not_6_out, in_1[3]);
  not not_7 (not_7_out, in_1[1]);
  not not_8 (not_8_out, in_1[3]);
  not not_9 (not_9_out, in_1[0]);
  not not_10 (not_10_out, in_1[2]);
  not not_11 (not_11_out, in_1[3]);
  not not_12 (not_12_out, in_1[2]);
  not not_13 (not_13_out, in_1[3]);
  not not_14 (not_14_out, in_1[2]);
  not not_15 (not_15_out, in_1[4]);
  not not_16 (not_16_out, in_1[3]);
  not not_17 (not_17_out, in_1[0]);
  not not_18 (not_18_out, in_1[3]);
  not not_19 (not_19_out, in_1[2]);
  not not_20 (not_20_out, in_1[4]);
  not not_21 (not_21_out, in_1[3]);
  not not_22 (not_22_out, in_1[3]);
  not not_23 (not_23_out, in_1[2]);
  not not_24 (not_24_out, in_1[2]);
  not not_25 (not_25_out, in_1[4]);
  not not_26 (not_26_out, in_1[0]);
  not not_27 (not_27_out, in_1[3]);
  not not_28 (not_28_out, in_1[2]);
  not not_29 (not_29_out, in_1[1]);
  not not_30 (not_30_out, in_1[0]);
  not not_31 (not_31_out, in_1[3]);
  not not_32 (not_32_out, in_1[1]);
  not not_33 (not_33_out, in_1[2]);
  not not_34 (not_34_out, in_1[3]);
  not not_35 (not_35_out, in_1[0]);
  and and_2 (and_2_out, not_1_out, in_1[3], in_1[2], in_1[1], in_1[0]);
  and and_3 (and_3_out, in_1[4], not_2_out, not_3_out, not_4_out, not_5_out);
  and and_4 (and_4_out, in_1[4], not_6_out, in_1[2], not_7_out, in_1[0]);
  and and_5 (and_5_out, in_1[4], not_8_out, in_1[2], in_1[1], not_9_out);
  and and_6 (and_6_out, in_1[3], not_10_out, in_1[1], in_1[0]);
  and and_7 (and_7_out, in_1[4], not_11_out, not_12_out, in_1[0]);
  and and_8 (and_8_out, in_1[4], not_13_out, not_14_out, in_1[1]);
  and and_9 (and_9_out, not_15_out, not_16_out, not_17_out);
  and and_10 (and_10_out, not_18_out, not_19_out, in_1[0]);
  and and_11 (and_11_out, not_20_out, not_21_out, in_1[1]);
  and and_12 (and_12_out, not_22_out, not_23_out, in_1[1]);
  and and_13 (and_13_out, not_24_out, in_1[1], in_1[0]);
  and and_14 (and_14_out, not_25_out, in_1[2], in_1[1], not_26_out);
  and and_15 (SIA, in_1[4], not_27_out, not_28_out, not_29_out, not_30_out);
  and and_16 (Rra, in_1[4], not_31_out, in_1[2], not_32_out, in_1[0]);
  and and_17 (li, in_1[4], in_1[3], not_33_out, in_1[1], in_1[0]);
  and and_18 (reboot, in_1[4], not_34_out, in_1[2], in_1[1], not_35_out);
  or or_1 (J, and_2_out, and_3_out, and_4_out, and_5_out);
  or or_2 (Asrc, and_6_out, and_7_out, and_8_out);
  or or_3 (RegW, and_9_out, and_10_out, and_11_out, and_12_out, and_13_out, and_14_out);
  and and_19 (store, in_1[0], ~in_1[1], in_1[2], in_1[3], ~in_1[4]);  // AND_Gate
  not not_36 (not_36_out, in_1[3]);
  not not_37 (not_37_out, in_1[1]);
  not not_38 (not_38_out, in_1[4]);
  not not_39 (not_39_out, in_1[3]);
  not not_40 (not_40_out, in_1[2]);
  not not_41 (not_41_out, in_1[1]);
  not not_42 (not_42_out, in_1[0]);
  not not_43 (not_43_out, in_1[3]);
  not not_44 (not_44_out, in_1[0]);
  not not_45 (not_45_out, in_1[4]);
  not not_46 (not_46_out, in_1[0]);
  not not_47 (not_47_out, in_1[4]);
  not not_48 (not_48_out, in_1[1]);
  and and_20 (and_20_out, not_36_out, in_1[2], not_37_out, in_1[0]);
  and and_21 (and_21_out, not_38_out, in_1[3], in_1[2], in_1[1], in_1[0]);
  and and_22 (and_22_out, in_1[4], not_39_out, not_40_out, not_41_out, not_42_out);
  and and_23 (and_23_out, in_1[4], not_43_out, in_1[2], in_1[1], not_44_out);
  and and_24 (DMR, not_45_out, in_1[3], in_1[2], in_1[1], not_46_out);
  and and_25 (DMW, not_47_out, in_1[3], in_1[2], not_48_out, in_1[0]);
  or or_4 (Brn, and_20_out, and_21_out, and_22_out, and_23_out);

  assign Aop = in_1[2:0];
endmodule

// Register
module Registers (
  input  write_signal,
  input  [2:0] Write_Register,
  input  [15:0] Write_Data,
  input  Clock,
  input  [2:0] R1,
  input  [2:0] R2,
  output [15:0] R1_value,
  output [15:0] R2_value
);

  wire and_1_out, and_2_out, and_3_out, and_4_out, and_5_out, and_6_out, and_7_out, and_8_out,
       decoder_1_out0, decoder_1_out1, decoder_1_out2, decoder_1_out3, decoder_1_out4, decoder_1_out5,
       decoder_1_out6, decoder_1_out7;
  wire [15:0] register_1_q, register_2_q, register_3_q, register_4_q, register_5_q, register_6_q,
       register_7_q, register_8_q;

  Decoder #(.select(3), .enable("false")) decoder_1 (
    .out0(decoder_1_out0), .out1(decoder_1_out1), .out2(decoder_1_out2), .out3(decoder_1_out3),
    .out4(decoder_1_out4), .out5(decoder_1_out5), .out6(decoder_1_out6), .out7(decoder_1_out7),
    .sel(Write_Register));
  and and_1 (and_1_out, write_signal, decoder_1_out0);
  and and_2 (and_2_out, write_signal, decoder_1_out1);
  and and_3 (and_3_out, write_signal, decoder_1_out2);
  and and_4 (and_4_out, write_signal, decoder_1_out3);
  and and_5 (and_5_out, write_signal, decoder_1_out4);
  and and_6 (and_6_out, write_signal, decoder_1_out5);
  and and_7 (and_7_out, write_signal, decoder_1_out6);
  and and_8 (and_8_out, write_signal, decoder_1_out7);
  Register #(.width(16)) register_1 (.D(Write_Data), .en(and_1_out), .Q(register_1_q), .clk(Clock));  // open: clr
  Register #(.width(16)) register_2 (.D(Write_Data), .en(and_2_out), .Q(register_2_q), .clk(Clock));  // open: clr
  Register #(.width(16)) register_3 (.D(Write_Data), .en(and_3_out), .Q(register_3_q), .clk(Clock));  // open: clr
  Register #(.width(16)) register_4 (.D(Write_Data), .en(and_4_out), .Q(register_4_q), .clk(Clock));  // open: clr
  Register #(.width(16)) register_5 (.D(Write_Data), .en(and_5_out), .Q(register_5_q), .clk(Clock));  // open: clr
  Register #(.width(16)) register_6 (.D(Write_Data), .en(and_6_out), .Q(register_6_q), .clk(Clock));  // open: clr
  Register #(.width(16)) register_7 (.D(Write_Data), .en(and_7_out), .Q(register_7_q), .clk(Clock));  // open: clr
  Register #(.width(16)) register_8 (.D(Write_Data), .en(and_8_out), .Q(register_8_q), .clk(Clock));  // open: clr
  Multiplexer #(.select(3), .width(16), .enable("false")) multiplexer_1 (
    .in0(register_1_q), .in1(register_2_q), .in2(register_3_q), .in3(register_4_q), .in4(register_5_q),
    .in5(register_6_q), .in6(register_7_q), .in7(register_8_q), .out(R1_value), .sel(R1));
  Multiplexer #(.select(3), .width(16), .enable("false")) multiplexer_2 (
    .in0(register_1_q), .in1(register_2_q), .in2(register_3_q), .in3(register_4_q), .in4(register_5_q),
    .in5(register_6_q), .in6(register_7_q), .in7(register_8_q), .out(R2_value), .sel(R2));
endmodule

module PC_Increment (
  input  [15:0] br,
  input  uncond,
  input  bnch,
  input  Rra,
  input  reboot,
  input  [15:0] ra,
  input  clock,
  input  cond,
  output [15:0] out_9,
  output [15:0] Ins
);

  wire register_2_q;
  wire [15:0] adder_2_out, adder_3_out, multiplexer_1_out, multiplexer_2_out, multiplexer_3_out,
       multiplexer_4_out, multiplexer_5_out, subtractor_1_out;

  Register #(.width(16), .trigger("falling")) register_1 (
    .D(multiplexer_5_out), .en(1'b1), .Q(Ins), .clk(clock));  // open: clr
  Adder #(.width(16)) adder_1 (.a(Ins), .b(16'h1), .out(out_9));  // open: cin, cout
  Multiplexer #(.width(16), .enable("false")) multiplexer_1 (
    .in0(out_9), .in1(Ins), .out(multiplexer_1_out), .sel(uncond));
  Subtractor #(.width(16)) subtractor_1 (.a(br), .b(16'h1), .out(subtractor_1_out));  // open: bin, bout
  Multiplexer #(.width(16), .enable("false")) multiplexer_2 (
    .in0(multiplexer_1_out), .in1(Ins), .out(multiplexer_2_out), .sel(register_2_q));
  Adder #(.width(16)) adder_2 (.a(Ins), .b(subtractor_1_out), .out(adder_2_out));  // open: cin, cout
  Multiplexer #(.width(16), .enable("false")) multiplexer_3 (
    .in0(multiplexer_2_out), .in1(adder_2_out), .out(multiplexer_3_out), .sel(bnch));
  Multiplexer #(.width(16), .enable("false")) multiplexer_4 (
    .in0(multiplexer_3_out), .in1(adder_3_out), .out(multiplexer_4_out), .sel(Rra));
  Adder #(.width(16)) adder_3 (.a(ra), .b(16'h1), .out(adder_3_out));  // open: cin, cout
  Register #(.width(1)) register_2 (.D(cond), .en(1'b1), .Q(register_2_q), .clk(clock));  // open: clr
  Multiplexer #(.width(16), .enable("false")) multiplexer_5 (
    .in0(multiplexer_4_out), .in1({16{1'b0}}), .out(multiplexer_5_out), .sel(reboot));
endmodule

module Divider (
  input  _1_bit,
  input  clock,
  input  in_3,
  input  in_4,
  input  in_5,
  input  in_6,
  input  in_7,
  input  [15:0] _16_bit,
  input  [2:0] _3_bit,
  input  [2:0] _3_bit_2,
  input  [4:0] _5_bit,
  input  [15:0] _16_bit_2,
  input  [15:0] _16_bit_3,
  output _1_bit_2,
  output out_15,
  output out_16,
  output out_17,
  output out_18,
  output out_19,
  output [15:0] out_20,
  output [2:0] out_21,
  output [2:0] out_22,
  output [4:0] out_23,
  output [15:0] out_24,
  output [15:0] out_25
);

  Register #(.width(1)) u__1_bit (.D(_1_bit), .Q(_1_bit_2), .clk(clock));  // open: en, clr
  Register #(.width(1)) register_1 (.D(in_3), .Q(out_15), .clk(clock));  // open: en, clr
  Register #(.width(1)) register_2 (.D(in_4), .Q(out_16), .clk(clock));  // open: en, clr
  Register #(.width(1)) register_3 (.D(in_5), .Q(out_17), .clk(clock));  // open: en, clr
  Register #(.width(1)) register_4 (.D(in_6), .Q(out_18), .clk(clock));  // open: en, clr
  Register #(.width(1)) register_5 (.D(in_7), .Q(out_19), .clk(clock));  // open: en, clr
  Register #(.width(16)) register_6 (.D(_16_bit), .Q(out_20), .clk(clock));  // open: en, clr
  Register #(.width(3)) register_7 (.D(_3_bit), .Q(out_21), .clk(clock));  // open: en, clr
  Register #(.width(3)) register_8 (.D(_3_bit_2), .Q(out_22), .clk(clock));  // open: en, clr
  Register #(.width(5)) register_9 (.D(_5_bit), .Q(out_23), .clk(clock));  // open: en, clr
  Register #(.width(16)) register_10 (.D(_16_bit_2), .Q(out_24), .clk(clock));  // open: en, clr
  Register #(.width(16)) register_11 (.D(_16_bit_3), .Q(out_25), .clk(clock));  // open: en, clr
endmodule

module J_cmd (
  input  [15:0] in_1,
  output uncond,
  output cond
);

  wire and_1_out, and_2_out, and_3_out, and_4_out, not_1_out, not_2_out, not_3_out, not_4_out, not_5_out,
       not_6_out, not_7_out, not_8_out, not_9_out, not_10_out;

  not not_1 (not_1_out, in_1[14]);
  not not_2 (not_2_out, in_1[12]);
  not not_3 (not_3_out, in_1[15]);
  not not_4 (not_4_out, in_1[14]);
  not not_5 (not_5_out, in_1[13]);
  not not_6 (not_6_out, in_1[12]);
  not not_7 (not_7_out, in_1[11]);
  not not_8 (not_8_out, in_1[15]);
  not not_9 (not_9_out, in_1[14]);
  not not_10 (not_10_out, in_1[12]);
  and and_1 (and_1_out, ~in_1[15], in_1[14], in_1[13], in_1[12], ~in_1[11]);  // AND_Gate
  and and_2 (and_2_out, not_1_out, in_1[13], not_2_out, in_1[11]);
  and and_3 (and_3_out, not_3_out, in_1[14], in_1[13], in_1[12], in_1[11]);
  and and_4 (and_4_out, in_1[15], not_4_out, not_5_out, not_6_out, not_7_out);
  and and_5 (cond, not_8_out, not_9_out, in_1[13], not_10_out, in_1[11]);
  or or_1 (uncond, and_1_out, and_2_out, and_3_out, and_4_out);
endmodule

module forwarding (
  input  [2:0] r1,
  input  [2:0] Dest,
  input  [2:0] r2,
  input  in_4,
  output r1_2,
  output r2_2
);

  wire comparator_1_eq, comparator_2_eq;

  Comparator #(.width(3)) comparator_1 (.a(r1), .b(Dest), .eq(comparator_1_eq));  // open: gt, lt
  Comparator #(.width(3)) comparator_2 (.a(Dest), .b(r2), .eq(comparator_2_eq));  // open: gt, lt
  and and_1 (r1_2, comparator_1_eq, in_4);
  and and_2 (r2_2, comparator_2_eq, in_4);
endmodule

module halter (
  input  [15:0] in_1,
  output h,
  output reboor
);

  and and_1 (h, in_1[15], in_1[14], in_1[13], in_1[12], in_1[11]);
  and and_2 (reboor, in_1[15], ~in_1[14], in_1[13], in_1[12], ~in_1[11]);  // AND_Gate
endmodule
